// Logisim project circuit.circ as structural Verilog: 1 circuit, main circuit main
module main (
  input  A_prime,
  input  B_prime,
  input  C_prime
);

  wire and_1_out, and_2_out, and_3_out, and_4_out, and_5_out, and_6_out, and_7_out, and_8_out, and_9_out,
       and_10_out, and_11_out, and_12_out, and_13_out, and_14_out, and_15_out, and_16_out, not_1_out,
       not_2_out, not_3_out, or_1_out, or_2_out, or_3_out, or_4_out, or_5_out, or_6_out, or_7_out;

  not not_1 (not_1_out, B_prime);
  not not_2 (not_2_out, A_prime);
  not not_3 (not_3_out, C_prime);
  and and_1 (and_1_out, A_prime, C_prime);
  and and_2 (and_2_out, not_2_out, not_3_out);
  and and_3 (and_3_out, B_prime, C_prime);
  and and_4 (and_4_out, not_1_out, not_3_out);
  and and_5 (and_5_out, B_prime, not_3_out);
  and and_6 (and_6_out, not_2_out, B_prime);
  and and_7 (and_7_out, not_2_out, not_3_out);
  and and_8 (and_8_out, A_prime, not_1_out, C_prime);
  and and_9 (and_9_out, B_prime, not_3_out);
  and and_10 (and_10_out, not_2_out, not_3_out);
  and and_11 (and_11_out, A_prime, not_1_out);
  and and_12 (and_12_out, A_prime, not_3_out);
  and and_13 (and_13_out, not_1_out, not_3_out);
  and and_14 (and_14_out, B_prime, not_3_out);
  and and_15 (and_15_out, A_prime, not_1_out);
  and and_16 (and_16_out, not_2_out, B_prime);
  or or_1 (or_1_out, and_1_out, B_prime, and_2_out);
  or or_2 (or_2_out, and_3_out, not_2_out, and_4_out);
  or or_3 (or_3_out, C_prime, A_prime, not_1_out);
  or or_4 (or_4_out, and_5_out, and_6_out, and_7_out, and_8_out);
  or or_5 (or_5_out, and_9_out, and_10_out);
  or or_6 (or_6_out, and_11_out, and_12_out, and_13_out);
  or or_7 (or_7_out, and_14_out, and_15_out, and_16_out);
  _7_Segment_Display u_7_segment_display_1 (
    .g(or_7_out), .f(or_6_out), .a(or_1_out), .b(or_2_out), .e(or_5_out), .d(or_4_out), .c(or_3_out));  // open: dp

  // Notes on the sheet:
  //   A
  //   C
  //   B
  //   a
  //   b
  //   c
  //   d
  //   e
  //   f
  //   g
endmodule
